# Fritzing sketch Therething Shield (saved by Fritzing 0.7.11b)
breadboards: 1

parts:
  U1 = HC-SR04 [chip_label=IC package="SIP (Single Inline) [THT]"]
  Arduino = Arduino
  R1 = Trimmer Potentiometer [maximum_resistance=10kΩ package=THT]
  R2 = 4.7k Ω Resistor [package=THT]
  LCD1 = LCD screen
  RE1 = Rotary Encoder [package=THT]
  S1 = Pushbutton [package="[THT]"]
  U2 = HC-SR04 [chip_label=IC package="SIP (Single Inline) [THT]"]

nets:
  VCC: U1.Vcc, Arduino.+5V, R1.leg2, R2.Pin_0, LCD1.VDD, S1.Pin_1, S1.Pin_2, U2.Vcc
  N1: U1.Trig, Arduino.A0
  N2: U1.Echo, Arduino.A1
  GND: U1.GND, Arduino.GND, R1.leg1, LCD1.VSS, LCD1.LED-, U2.GND
  N3: Arduino.D12, S1.Pin_3, S1.Pin_4
  N4: Arduino.D11, LCD1.RS
  N5: Arduino.D10, LCD1.R/W
  N6: Arduino.D9, LCD1.E
  N7: Arduino.D8, LCD1.DB4
  N8: Arduino.D7, LCD1.DB5
  N9: Arduino.D6, LCD1.DB6
  N10: Arduino.D5, LCD1.DB7
  N11: Arduino.D4, RE1.EncoderPinB
  N12: Arduino.D3, RE1.EncoderPinC
  N13: Arduino.D2, RE1.EncoderPinA
  N14: Arduino.A2, U2.Trig
  N15: Arduino.A3, U2.Echo
  N16: R1.wiper, LCD1.V0
  N17: R2.Pin_1, LCD1.LED+

custom parts:
  HC-SR04: HC-SR04 ultrasound distance sensor
